# Fritzing sketch AP - Antipanico (saved by Fritzing 0.9.3b)
circuit board: 10cm x 6cm
stripboards: 1

parts:
  R1 = Resistor [tolerance=±5% resistance=10k package=THT]
  Teensy_3_5 = Teensy 3.1
  S1 = SWITCH-MOMENTARY-2 [package=tactile-switch-1101ne]
  J15 = Camdenboss CTB0158-2 [part_number=CTB0158-2 package=THT]
  J18 = screw terminal, 3 pins
  J19 = Camdenboss CTB0158-2 [part_number=CTB0158-2 package=THT]
  R2 = Resistor [tolerance=±5% resistance=10k package=THT]
  KY-1 = Keyes Relay [package=THT]

nets:
  N1: R1.Pin_0, Teensy_3_5.AGND, J18.pin2, R2.Pin_0, KY-1.ground
  N2: R1.Pin_1, Teensy_3_5.A2/D16, S1.2, J19.pin2
  N3: Teensy_3_5.GND, Teensy_3_5.A0/D14, Teensy_3_5.A1/D15, Teensy_3_5.A3/D17, Teensy_3_5.A4/D18, Teensy_3_5.A5/D19, Teensy_3_5.A6/D20, Teensy_3_5.A7/D21, Teensy_3_5.A8/D22, Teensy_3_5.A9/D23
  N4: Teensy_3_5.D0, Teensy_3_5.D1, Teensy_3_5.D2, Teensy_3_5.D3, Teensy_3_5.D4, Teensy_3_5.D5, Teensy_3_5.D6, Teensy_3_5.D7, Teensy_3_5.D8
  N5: Teensy_3_5.3V3, S1.1, J19.pin1
  N6: J15.pin1, R2.Pin_1
  N7: J15.pin2, J18.pin3, KY-1.signal
  N8: J18.pin1, KY-1.power

notes:
  USB 5V
  segnale chiusura porta

custom parts:
  Keyes Relay: The Keyes 5V relay module is suitable for SCM development, home appliance control. It uses a 5V~12V TIL control signal which can control DC / AC signal.
