# Fritzing sketch G7 - Portafrutta (saved by Fritzing 0.9.3b)
stripboards: 1

parts:
  Componente3 = HX711 Weighing Sensor Module
  Componente1 = HX711 Weighing Sensor Module
  Componente2 = HX711 Weighing Sensor Module
  Componente4 = Arduino Uno (Rev3)
  J15 = screw terminal, 4 pins
  J16 = screw terminal, 4 pins
  J17 = screw terminal, 4 pins

nets:
  VCC: Componente3.VCC, Componente1.VCC, Componente2.VCC, Componente4.5V, J15.pin4, J16.pin4, J17.pin4
  GND: Componente3.GND, Componente1.GND, Componente2.GND, Componente4.GND, J15.pin1, J16.pin1, J17.pin1
  N1: Componente3.DO/RX, Componente4.D2, J15.pin2
  N2: Componente3.CK/TX, Componente1.CK/TX, Componente2.CK/TX, Componente4.D3_PWM, J15.pin3, J16.pin3, J17.pin3
  N3: Componente1.DO/RX, Componente4.D5_PWM, J17.pin2
  N4: Componente2.DO/RX, Componente4.D4, J16.pin2

notes:
  Load Cell
